# Fritzing sketch iot_schematic (saved by Fritzing 0.9.3b)
circuit board: 8.46667cm x 5.64444cm
breadboards: 1

parts:
  Raspberry_Pi = Raspberry Pi B+
  R = Resistor [tolerance=±5% resistance=220 package=THT]
  LED = LED - 3mm [color="Red (635nm)" package="3 mm [THT]"]

nets (from the schematic view):
  N1: Raspberry_Pi.GND, LED.cathode
  N2: Raspberry_Pi.GIPO16, R.Pin_0
  N3: R.Pin_1, LED.anode
